// Logisim project forwarding.circ as structural Verilog: 5 circuits, main circuit main
module main (
  input  [4:0] reg__3__write,
  input  [31:0] rs,
  input  [31:0] rt,
  input  ALU_Src,
  input  [31:0] imm,
  input  [4:0] reg__1,
  input  [4:0] reg__2,
  input  [3:0] ALU_Control,
  output [31:0] RESULTADO_FINAL
);

  wire Clock_out, Forward_A, Forward_B;
  wire [4:0] ex_mem_1_reg__3__write_2, id_ex_1_reg__1_2, id_ex_1_reg__2_2, id_ex_1_reg__3__write_2;
  wire [31:0] alu_1_result, id_ex_1_imm_2, id_ex_1_rs_2, id_ex_1_rt_2, multiplexer_1_out, multiplexer_2_out,
       multiplexer_3_out;

  Clock Clock (.out(Clock_out));
  ID_EX id_ex_1 (
    .rs(rs), .CLK(Clock_out), .rs_2(id_ex_1_rs_2), .rt(rt), .rt_2(id_ex_1_rt_2), .imm(imm),
    .imm_2(id_ex_1_imm_2), .reg__1(reg__1), .reg__1_2(id_ex_1_reg__1_2), .reg__2(reg__2),
    .reg__2_2(id_ex_1_reg__2_2), .reg__3__write(reg__3__write), .reg__3__write_2(id_ex_1_reg__3__write_2));
  Multiplexer #(.width(32), .enable("false")) multiplexer_1 (
    .in0(id_ex_1_rs_2), .in1(RESULTADO_FINAL), .out(multiplexer_1_out), .sel(Forward_A));
  Multiplexer #(.width(32), .enable("false")) multiplexer_2 (
    .in0(id_ex_1_rt_2), .in1(RESULTADO_FINAL), .out(multiplexer_2_out), .sel(Forward_B));
  Multiplexer #(.width(32), .enable("false")) multiplexer_3 (
    .in0(multiplexer_2_out), .in1(id_ex_1_imm_2), .out(multiplexer_3_out), .sel(ALU_Src));
  Forwarding_Unit forwarding_unit_1 (
    .reg__1__ID_EX(id_ex_1_reg__1_2), .reg__3__EX_MEM(ex_mem_1_reg__3__write_2), .Forward_A(Forward_A),
    .Forward_B(Forward_B), .reg__2__ID_EX(id_ex_1_reg__2_2));
  ALU alu_1 (.A(multiplexer_1_out), .B(multiplexer_3_out), .Result(alu_1_result), .ALU_Control(ALU_Control));
  EX_MEM ex_mem_1 (
    .ALU_result(alu_1_result), .ALU_result_2(RESULTADO_FINAL), .CLK(Clock_out),
    .reg__3__write(id_ex_1_reg__3__write_2), .reg__3__write_2(ex_mem_1_reg__3__write_2));

  // Notes on the sheet:
  //   ID/EX
  //   Resultado a forwardear
  //   A
  //   B
  //   rs
  //   rt
  //   ALU
  //   Forwarding Unit
  //   result
  //   EX/MEM
  //   Este es el registro donde va el resultado en WB
  //   (el número de registro)
endmodule

module ID_EX (
  input  [4:0] reg__3__write,
  input  [31:0] rs,
  input  [31:0] rt,
  input  CLK,
  input  [31:0] imm,
  input  [4:0] reg__1,
  input  [4:0] reg__2,
  output [4:0] reg__3__write_2,
  output [31:0] rs_2,
  output [31:0] rt_2,
  output [31:0] imm_2,
  output [4:0] reg__1_2,
  output [4:0] reg__2_2
);

  Register #(.width(32)) register_1 (.D(rs), .Q(rs_2), .clk(CLK));  // open: en, clr
  Register #(.width(32)) register_2 (.D(rt), .Q(rt_2), .clk(CLK));  // open: en, clr
  Register #(.width(32)) register_3 (.D(imm), .Q(imm_2), .clk(CLK));  // open: en, clr
  Register #(.width(5)) register_4 (.D(reg__1), .Q(reg__1_2), .clk(CLK));  // open: en, clr
  Register #(.width(5)) register_5 (.D(reg__2), .Q(reg__2_2), .clk(CLK));  // open: en, clr
  Register #(.width(5)) register_6 (.D(reg__3__write), .Q(reg__3__write_2), .clk(CLK));  // open: en, clr
endmodule

module ALU (
  input  [31:0] A,
  input  [31:0] B,
  input  [3:0] ALU_Control,
  output [31:0] Result
);

  wire [31:0] adder_1_out, and_1_out, multiplexer_1_out, multiplexer_2_out, not_1_out, not_2_out, or_1_out;

  assign not_1_out = ~A;  // NOT_Gate not_1, 32 bits wide
  Multiplexer #(.width(32), .enable("false")) multiplexer_1 (
    .in0(B), .in1(not_2_out), .out(multiplexer_1_out), .sel(ALU_Control[2]));
  assign not_2_out = ~B;  // NOT_Gate not_2, 32 bits wide
  Multiplexer #(.width(32), .enable("false")) multiplexer_2 (
    .in0(A), .in1(not_1_out), .out(multiplexer_2_out), .sel(ALU_Control[3]));
  assign and_1_out = multiplexer_2_out & multiplexer_1_out;  // AND_Gate and_1, 32 bits wide
  assign or_1_out = multiplexer_2_out | multiplexer_1_out;  // OR_Gate or_1, 32 bits wide
  Adder #(.width(32)) adder_1 (
    .a(multiplexer_2_out), .b(multiplexer_1_out), .out(adder_1_out), .cin(ALU_Control[2]));  // open: cout
  Multiplexer #(.select(2), .width(32), .enable("false")) multiplexer_3 (
    .in0(and_1_out), .in1(or_1_out), .in2(adder_1_out), .out(Result), .sel(ALU_Control[1:0]));  // open: in3

  // Other names for the same wires on the sheet: Operation[1:0] = ALU_Control[1:0]; B_Invert = ALU_Control[2];
  //   Carry_In = ALU_Control[2]; A_Invert = ALU_Control[3]
endmodule

module EX_MEM (
  input  [4:0] reg__3__write,
  input  [31:0] ALU_result,
  input  CLK,
  output [4:0] reg__3__write_2,
  output [31:0] ALU_result_2
);

  Register #(.width(5)) register_1 (.D(reg__3__write), .Q(reg__3__write_2), .clk(CLK));  // open: en, clr
  Register #(.width(32)) register_2 (.D(ALU_result), .Q(ALU_result_2), .clk(CLK));  // open: en, clr
endmodule

module Forwarding_Unit (
  input  [4:0] reg__1__ID_EX,
  input  [4:0] reg__3__EX_MEM,
  input  [4:0] reg__2__ID_EX,
  output Forward_A,
  output Forward_B
);

  wire xnor_1_out, xnor_2_out, xnor_3_out, xnor_4_out, xnor_5_out, xnor_6_out, xnor_7_out, xnor_8_out,
       xnor_9_out, xnor_10_out;

  xnor xnor_1 (xnor_1_out, reg__1__ID_EX[0], reg__3__EX_MEM[0]);
  xnor xnor_2 (xnor_2_out, reg__1__ID_EX[1], reg__3__EX_MEM[1]);
  xnor xnor_3 (xnor_3_out, reg__1__ID_EX[2], reg__3__EX_MEM[2]);
  xnor xnor_4 (xnor_4_out, reg__1__ID_EX[3], reg__3__EX_MEM[3]);
  xnor xnor_5 (xnor_5_out, reg__1__ID_EX[4], reg__3__EX_MEM[4]);
  xnor xnor_6 (xnor_6_out, reg__3__EX_MEM[0], reg__2__ID_EX[0]);
  xnor xnor_7 (xnor_7_out, reg__3__EX_MEM[1], reg__2__ID_EX[1]);
  xnor xnor_8 (xnor_8_out, reg__3__EX_MEM[2], reg__2__ID_EX[2]);
  xnor xnor_9 (xnor_9_out, reg__3__EX_MEM[3], reg__2__ID_EX[3]);
  xnor xnor_10 (xnor_10_out, reg__3__EX_MEM[4], reg__2__ID_EX[4]);
  and and_1 (Forward_A, xnor_1_out, xnor_2_out, xnor_3_out, xnor_4_out, xnor_5_out);
  and and_2 (Forward_B, xnor_6_out, xnor_7_out, xnor_8_out, xnor_9_out, xnor_10_out);
endmodule
